// Logisim project s-mips.circ as structural Verilog: 20 circuits, main circuit S-MIPS Board
module S_MIPS_Board (
  output halt
);

  wire button_1_out, CLK, CS, d_ff_1_q, R_W, Reset_out, RST, TTY_EN;
  wire [2:0] KDB;
  wire [3:0] Mask, ram_1_read_time, ram_1_write_time;
  wire [6:0] KDB_DATA, TTY_DATA;
  wire [15:0] Addr;
  wire [31:0] ram_1_data_out_0, ram_1_data_out_1, ram_1_data_out_2, ram_1_data_out_3, s_mips_1_ram_in_0,
       s_mips_1_ram_in_1, s_mips_1_ram_in_2, s_mips_1_ram_in_3;

  TTY #(.rows(25), .cols(80)) tty_1 (.data(TTY_DATA), .clk(CLK), .we(TTY_EN), .clr(RST));
  RAM ram_1 (
    .Address(Addr), .Data_Out_0(ram_1_data_out_0), .Data_Out_1(ram_1_data_out_1),
    .Data_Out_2(ram_1_data_out_2), .Data_Out_3(ram_1_data_out_3), .Data_In_0(s_mips_1_ram_in_0),
    .Data_In_1(s_mips_1_ram_in_1), .Data_In_2(s_mips_1_ram_in_2), .Data_In_3(s_mips_1_ram_in_3), .Mask(Mask),
    .nRead_Write(R_W), .Chip_Select(CS), .Read_Time(ram_1_read_time), .Reset(button_1_out),
    .Write_Time(ram_1_write_time));
  Button button_1 (.out(button_1_out));
  Keyboard #(.buflen(64)) keyboard_1 (.clk(CLK), .re(KDB[0]), .avail(KDB[2]), .data(KDB_DATA));  // open: clr
  S_MIPS s_mips_1 (
    .Kbd_Enable(KDB[0]), .Address(Addr), .Kbd_Clear(KDB[1]), .Kbd_Available(KDB[2]),
    .RAM_In_0(s_mips_1_ram_in_0), .Kbd_ASCII_Data(KDB_DATA), .RAM_In_1(s_mips_1_ram_in_1),
    .TTY_Enable(TTY_EN), .RAM_In_2(s_mips_1_ram_in_2), .RAM_In_3(s_mips_1_ram_in_3),
    .TTY_ASCII_Data(TTY_DATA), .Reset(RST), .RAM_Out_0(ram_1_data_out_0), .Clock(CLK),
    .RAM_Out_1(ram_1_data_out_1), .Stop(halt), .RAM_Out_2(ram_1_data_out_2), .RAM_Out_3(ram_1_data_out_3),
    .Mask(Mask), .Read_Time(ram_1_read_time), .Write_Time(ram_1_write_time), .nRead_Write(R_W),
    .Chip_Select(CS));
  D_Flip_Flop d_ff_1 (.clk(CLK), .D(1'b1), .Q(d_ff_1_q), .reset(Reset_out));  // open: Qn, preset, en
  Button Reset (.out(Reset_out));
  Clock clock_1 (.out(CLK));
  D_Flip_Flop d_ff_2 (.clk(CLK), .D(d_ff_1_q), .Qn(RST), .reset(Reset_out));  // open: Q, preset, en

  // Notes on the sheet:
  //   NO MODIFICAR
  //   Keyboard
endmodule

module RAM (
  input  [15:0] Address,
  input  [31:0] Data_In_0,
  input  [31:0] Data_In_1,
  input  [31:0] Data_In_2,
  input  [31:0] Data_In_3,
  input  [3:0] Mask,
  input  nRead_Write,
  input  Chip_Select,
  input  Reset,
  output [31:0] Data_Out_0,
  output [31:0] Data_Out_1,
  output [31:0] Data_Out_2,
  output [31:0] Data_Out_3,
  output [3:0] Read_Time,
  output [3:0] Write_Time
);

  wire and_2_out, and_3_out, and_4_out, and_5_out, and_6_out, and_7_out, and_8_out, and_9_out, Changed, CLK,
       comparator_2_eq, comparator_3_eq, comparator_4_eq, comparator_5_eq, comparator_6_eq, Count,
       demultiplexer_3_out0, Idle, Idle_q, Load, Load0, Load1, nand_1_out, or_1_out, or_2_out, or_3_out,
       or_4_out, or_5_out, or_6_out, or_7_out, or_8_out, or_9_out, or_10_out, Proc_q, Update_Mem, Zero_Time;
  wire [3:0] counter_1_q, multiplexer_1_out, subtractor_1_out;
  wire [31:0] register_1_q, register_2_q, register_3_q, register_4_q, register_5_q;

  // Probe on 4'b0011
  // Probe on 4'b0101
  Multiplexer_part #(.width(4), .enable("false")) multiplexer_1 (
    .in0(4'b0011), .in1(4'b0101), .out(multiplexer_1_out), .sel(nRead_Write));
  or or_1 (or_1_out, Idle, Update_Mem);
  or or_2 (or_2_out, ~Chip_Select, Reset);  // OR_Gate
  Subtractor #(.width(4)) subtractor_1 (.a(multiplexer_1_out), .b(4'b0010), .out(subtractor_1_out));  // open: bin, bout
  D_Flip_Flop u_Idle (.clk(CLK), .D(or_1_out), .Q(Idle_q), .preset(or_2_out));  // open: Qn, en, reset
  Demultiplexer #(.enable("false")) demultiplexer_1 (.out0(Idle), .out1(Load0), .in(Idle_q), .sel(Changed));
  // Probe on counter_1_q
  Counter #(.width(4), .max('hf)) counter_1 (
    .load(Load), .D(subtractor_1_out), .count(Count), .Q(counter_1_q), .clk(CLK), .clr(or_3_out));  // open: carry
  or or_3 (or_3_out, ~Chip_Select, Reset);  // OR_Gate
  Comparator #(.width(4), .mode("unsigned")) comparator_1 (
    .a(4'b0000), .b(counter_1_q), .eq(Zero_Time));  // open: gt, lt
  or or_4 (or_4_out, Count, Load0, Load1);
  Register #(.width(32)) register_1 (.D(Data_In_0), .en(Chip_Select), .Q(register_1_q), .clk(CLK), .clr(or_5_out));
  or or_5 (or_5_out, ~Chip_Select, Reset);  // OR_Gate
  Register #(.width(32)) register_2 (.D(Data_In_1), .en(Chip_Select), .Q(register_2_q), .clk(CLK), .clr(or_6_out));
  or or_6 (or_6_out, ~Chip_Select, Reset);  // OR_Gate
  Register #(.width(32)) register_3 (.D(Data_In_2), .en(Chip_Select), .Q(register_3_q), .clk(CLK), .clr(or_7_out));
  or or_7 (or_7_out, ~Chip_Select, Reset);  // OR_Gate
  Register #(.width(32)) register_4 (.D(Data_In_3), .en(Chip_Select), .Q(register_4_q), .clk(CLK), .clr(or_8_out));
  or or_8 (or_8_out, ~Chip_Select, Reset);  // OR_Gate
  Register #(.width(32)) register_5 (
    .D({{11{1'b1}}, nRead_Write, Mask, Address}), .en(Chip_Select), .Q(register_5_q), .clk(CLK),
    .clr(or_9_out));
  or or_9 (or_9_out, ~Chip_Select, Reset);  // OR_Gate
  D_Flip_Flop Proc (.clk(CLK), .D(or_4_out), .Q(Proc_q), .reset(or_10_out));  // open: Qn, preset, en
  or or_10 (or_10_out, ~Chip_Select, Reset);  // OR_Gate
  Demultiplexer #(.enable("false")) demultiplexer_2 (
    .out0(Count), .out1(Update_Mem), .in(demultiplexer_3_out0), .sel(Zero_Time));
  Demultiplexer #(.enable("false")) demultiplexer_3 (
    .out0(demultiplexer_3_out0), .out1(Load1), .in(Proc_q), .sel(Changed));
  Clock clock_1 (.out(CLK));
  Comparator #(.width(32)) comparator_2 (.a(register_1_q), .b(Data_In_0), .eq(comparator_2_eq));  // open: gt, lt
  Comparator #(.width(32)) comparator_3 (.a(register_2_q), .b(Data_In_1), .eq(comparator_3_eq));  // open: gt, lt
  Comparator #(.width(32)) comparator_4 (.a(register_3_q), .b(Data_In_2), .eq(comparator_4_eq));  // open: gt, lt
  Comparator #(.width(32)) comparator_5 (.a(register_4_q), .b(Data_In_3), .eq(comparator_5_eq));  // open: gt, lt
  Comparator #(.width(32)) comparator_6 (
    .a(register_5_q), .b({{11{1'b1}}, nRead_Write, Mask, Address}), .eq(comparator_6_eq));  // open: gt, lt
  nand nand_1 (nand_1_out, comparator_6_eq, comparator_2_eq, comparator_3_eq, comparator_4_eq, comparator_5_eq);
  and and_1 (Changed, nand_1_out, Chip_Select);
  or or_11 (Load, Count, Load1, Load0);
  and and_2 (and_2_out, Mask[0], Update_Mem, nRead_Write);
  and and_3 (and_3_out, Mask[1], Update_Mem, nRead_Write);
  and and_4 (and_4_out, Mask[2], Update_Mem, nRead_Write);
  and and_5 (and_5_out, Mask[3], Update_Mem, nRead_Write);
  RAM_part #(.addrWidth(16), .dataWidth(32), .bus("separate")) ram_1 (
    .addr(Address), .din(Data_In_0), .data(Data_Out_0), .str(and_2_out), .sel(Chip_Select), .clk(CLK),
    .ld(and_6_out), .clr(Reset));
  and and_6 (and_6_out, ~nRead_Write, Idle);  // AND_Gate
  RAM_part #(.addrWidth(16), .dataWidth(32), .bus("separate")) ram_2 (
    .addr(Address), .din(Data_In_1), .data(Data_Out_1), .str(and_3_out), .sel(Chip_Select), .clk(CLK),
    .ld(and_7_out), .clr(Reset));
  and and_7 (and_7_out, ~nRead_Write, Idle);  // AND_Gate
  RAM_part #(.addrWidth(16), .dataWidth(32), .bus("separate")) ram_3 (
    .addr(Address), .din(Data_In_2), .data(Data_Out_2), .str(and_4_out), .sel(Chip_Select), .clk(CLK),
    .ld(and_8_out), .clr(Reset));
  and and_8 (and_8_out, ~nRead_Write, Idle);  // AND_Gate
  RAM_part #(.addrWidth(16), .dataWidth(32), .bus("separate")) ram_4 (
    .addr(Address), .din(Data_In_3), .data(Data_Out_3), .str(and_5_out), .sel(Chip_Select), .clk(CLK),
    .ld(and_9_out), .clr(Reset));
  and and_9 (and_9_out, ~nRead_Write, Idle);  // AND_Gate

  assign Read_Time = 4'b0011;
  assign Write_Time = 4'b0101;

  // Other names for the same wires on the sheet: M0 = Mask[0]; M1 = Mask[1]; M2 = Mask[2]; M3 = Mask[3];
  //   RW = nRead_Write; CLR = Reset; CS = Chip_Select; Load2 = Count

  // Notes on the sheet:
  //   NO MODIFICAR
  //   excepto quizás los valores RT y WT
  //   BANK0
  //   BANK1
  //   BANK2
  //   BANK3
endmodule

module S_MIPS (
  input  Kbd_Available,
  input  [6:0] Kbd_ASCII_Data,
  input  [31:0] RAM_Out_0,
  input  [31:0] RAM_Out_1,
  input  Reset,
  input  [31:0] RAM_Out_2,
  input  Clock,
  input  [31:0] RAM_Out_3,
  input  [3:0] Read_Time,
  input  [3:0] Write_Time,
  output Kbd_Enable,
  output [15:0] Address,
  output Kbd_Clear,
  output TTY_Enable,
  output [6:0] TTY_ASCII_Data,
  output Stop,
  output [31:0] RAM_In_0,
  output [31:0] RAM_In_1,
  output [31:0] RAM_In_2,
  output [31:0] RAM_In_3,
  output [3:0] Mask,
  output nRead_Write,
  output Chip_Select
);

  wire chk, CLK, control_unit_1_next, CS1, CS2, Data_Done, data_path_1_add, data_path_1_addi,
       data_path_1_and, data_path_1_andi, data_path_1_beq, data_path_1_bgtz, data_path_1_blez,
       data_path_1_bltz, data_path_1_bne, data_path_1_div, data_path_1_divu, data_path_1_done,
       data_path_1_halt, data_path_1_j, data_path_1_jr, data_path_1_kbd, data_path_1_lw, data_path_1_mfhi,
       data_path_1_mflo, data_path_1_mult, data_path_1_mulu, data_path_1_nop, data_path_1_nor,
       data_path_1_or, data_path_1_ori, data_path_1_pop, data_path_1_push, data_path_1_rnd, data_path_1_slt,
       data_path_1_slti, data_path_1_sltiu, data_path_1_sltu, data_path_1_sub, data_path_1_sw,
       data_path_1_tty, data_path_1_xor, data_path_1_xori, End, enInst, enRead, enRnd, enSP, enWrite, goInst,
       popRF, pushRF, Read_Done, Write_Done;
  wire [15:0] Instruction_Address, multiplexer_1_out, Read_Address, Write_Address;
  wire [31:0] CACHE_OUT_0, CACHE_OUT_1, CACHE_OUT_2, CACHE_OUT_3, Data, Dir, PC, RAM_Data;

  or or_1 (Chip_Select, CS1, CS2, nRead_Write);
  Multiplexer_part #(.width(16), .enable("false")) multiplexer_1 (
    .in0(Read_Address), .in1(Write_Address), .out(multiplexer_1_out), .sel(enWrite));
  and and_1 (CLK, Clock, ~Stop);  // AND_Gate
  or or_2 (Data_Done, Write_Done, Read_Done);
  Multiplexer_part #(.width(16), .enable("false")) multiplexer_2 (
    .in0(multiplexer_1_out), .in1(Instruction_Address), .out(Address), .sel(CS1));
  Read_RAM read_ram_1 (
    .Direction(Dir), .Clock(CLK), .Reset(Reset), .Enable(enRead), .Read_Time(Read_Time),
    .RAM_Output_0(RAM_Out_0), .RAM_Output_1(RAM_Out_1), .RAM_Output_2(RAM_Out_2), .RAM_Output_3(RAM_Out_3),
    .Address(Read_Address), .Chip_Select(CS2), .Done(Read_Done), .RAM_Output(RAM_Data));
  Data_Path data_path_1 (
    .Clock(CLK), .Kbd_ASCII_Data(Kbd_ASCII_Data), .Cache_Out_0(CACHE_OUT_0), .Cache_Out_1(CACHE_OUT_1),
    .Reset(Reset), .Kbd_Available(Kbd_Available), .Next(control_unit_1_next), .enable_Random(enRnd),
    .enable_Write(enWrite), .Cache_Out_2(CACHE_OUT_2), .Cache_Out_3(CACHE_OUT_3), .push_RF(pushRF),
    .enable_Read(enRead), .pop_RF(popRF), .enable_SP(enSP), .Read_Done(Read_Done), .RAM_Data(RAM_Data),
    .enable_Instr(enInst), .Write_Done(Write_Done), .PC(PC), .Direction(Dir), .nop(data_path_1_nop),
    .\and (data_path_1_and), .beq(data_path_1_beq), .slt(data_path_1_slt), .add(data_path_1_add),
    .\or (data_path_1_or), .bne(data_path_1_bne), .sltu(data_path_1_sltu), .sub(data_path_1_sub),
    .\nor (data_path_1_nor), .blez(data_path_1_blez), .slti(data_path_1_slti), .mult(data_path_1_mult),
    .\xor (data_path_1_xor), .bgtz(data_path_1_bgtz), .sltiu(data_path_1_sltiu), .mulu(data_path_1_mulu),
    .andi(data_path_1_andi), .bltz(data_path_1_bltz), .div(data_path_1_div), .ori(data_path_1_ori),
    .j(data_path_1_j), .lw(data_path_1_lw), .divu(data_path_1_divu), .xori(data_path_1_xori),
    .jr(data_path_1_jr), .sw(data_path_1_sw), .addi(data_path_1_addi), .mfhi(data_path_1_mfhi),
    .halt(data_path_1_halt), .mflo(data_path_1_mflo), .tty(data_path_1_tty), .pop(data_path_1_pop),
    .rnd(data_path_1_rnd), .push(data_path_1_push), .kbd(data_path_1_kbd), .Done(data_path_1_done),
    .Data(Data), .Go_Instruction(goInst), .End(End), .Check(chk), .TTY_Data(TTY_ASCII_Data));
  Instruction_Cache instruction_cache_1 (
    .Instruction_Address(PC), .RAM_Output_0(RAM_Out_0), .RAM_Output_1(RAM_Out_1), .RAM_Output_2(RAM_Out_2),
    .RAM_Output_3(RAM_Out_3), .Clock(CLK), .Reset(Reset), .Enable(goInst), .Read_Time(Read_Time),
    .Cache_Out_0(CACHE_OUT_0), .Cache_Out_1(CACHE_OUT_1), .Cache_Out_2(CACHE_OUT_2),
    .Cache_Out_3(CACHE_OUT_3), .RAM_Address(Instruction_Address), .Chip_Select(CS1), .Finish(End),
    .Data(Data), .Address(Dir), .Check(chk));
  Write_RAM write_ram_1 (
    .Direction(Dir), .Clock(CLK), .Reset(Reset), .Enable(enWrite), .Write_Time(Write_Time), .Data(Data),
    .Mask(Mask), .Chip_Select(nRead_Write), .Done(Write_Done), .Address(Write_Address),
    .RAM_Output_0(RAM_In_0), .RAM_Output_1(RAM_In_1), .RAM_Output_2(RAM_In_2), .RAM_Output_3(RAM_In_3));
  Control_Unit control_unit_1 (
    .Data_Done(Data_Done), .Instruction_Done(data_path_1_done), .Clock(CLK), .nop(data_path_1_nop),
    .add(data_path_1_add), .Next(control_unit_1_next), .sub(data_path_1_sub), .mult(data_path_1_mult),
    .enable_Random(enRnd), .mulu(data_path_1_mulu), .div(data_path_1_div), .STOP(Stop),
    .divu(data_path_1_divu), .addi(data_path_1_addi), .enable_Read(enRead), .\and (data_path_1_and),
    .enable_Write(enWrite), .\or (data_path_1_or), .\nor (data_path_1_nor), .push_RF(pushRF),
    .\xor (data_path_1_xor), .andi(data_path_1_andi), .pop_RF(popRF), .ori(data_path_1_ori),
    .xori(data_path_1_xori), .enSP(enSP), .beq(data_path_1_beq), .enable_Instr(enInst),
    .bne(data_path_1_bne), .blez(data_path_1_blez), .enable_TTY(TTY_Enable), .bgtz(data_path_1_bgtz),
    .bltz(data_path_1_bltz), .enable_KBD(Kbd_Enable), .j(data_path_1_j), .jr(data_path_1_jr),
    .slt(data_path_1_slt), .sltu(data_path_1_sltu), .slti(data_path_1_slti), .sltiu(data_path_1_sltiu),
    .lw(data_path_1_lw), .sw(data_path_1_sw), .mfhi(data_path_1_mfhi), .mflo(data_path_1_mflo),
    .pop(data_path_1_pop), .push(data_path_1_push), .halt(data_path_1_halt), .tty(data_path_1_tty),
    .rnd(data_path_1_rnd), .kbd(data_path_1_kbd));

  assign Kbd_Clear = Reset;

  // Other names for the same wires on the sheet: CS = Chip_Select; KBD_AVAIL = Kbd_Available; CLR = Reset;
  //   KBD_CLR = Reset; KBD_DATA[6:0] = Kbd_ASCII_Data; RAM_A[15:0] = Address; RAM_INPUT_0[31:0] = RAM_In_0;
  //   RAM_INPUT_1[31:0] = RAM_In_1; RAM_INPUT_2[31:0] = RAM_In_2; RAM_INPUT_3[31:0] = RAM_In_3; RAM_MASK[3:0] = Mask;
  //   RAM_OUTPUT_0[31:0] = RAM_Out_0; RAM_OUTPUT_1[31:0] = RAM_Out_1; RAM_OUTPUT_2[31:0] = RAM_Out_2;
  //   RAM_OUTPUT_3[31:0] = RAM_Out_3; CS3 = nRead_Write; RW = nRead_Write; TTY_DATA[6:0] = TTY_ASCII_Data

  // Notes on the sheet:
  //   RAM ADDRESS
  //   DATA FROM RAM
  //   DATA TO RAM
  //   DATA WRITE MASK
  //   RAM TIMING
  //   RAM CONTROL
  //   KEYBOARD
  //   TTY
  //   SEQUENCING
endmodule

module Instruction_Cache (
  input  [31:0] Instruction_Address,
  input  [31:0] RAM_Output_0,
  input  [31:0] RAM_Output_1,
  input  [31:0] RAM_Output_2,
  input  [31:0] RAM_Output_3,
  input  Clock,
  input  Reset,
  input  Enable,
  input  Check,
  input  [3:0] Read_Time,
  input  [31:0] Data,
  input  [31:0] Address,
  output [31:0] Cache_Out_0,
  output [31:0] Cache_Out_1,
  output [31:0] Cache_Out_2,
  output [31:0] Cache_Out_3,
  output [15:0] RAM_Address,
  output Finish,
  output Chip_Select
);

  wire C__0, ChipS1, ChipS2, decoder_1_out0, decoder_1_out1, decoder_1_out2, decoder_1_out3, decoder_2_out0,
       decoder_2_out1, decoder_2_out2, decoder_2_out3, decoder_2_out4, decoder_2_out5, decoder_2_out6,
       decoder_2_out7, demultiplexer_1_out0, demultiplexer_1_out1, demultiplexer_2_out0,
       demultiplexer_2_out1, eqTag, L, or_2_out, or_3_out, or_4_out, or_5_out, or_6_out, READ_q, selD,
       START_q, str0, str1, str2, str3, V0, V1, V2, V3, V4, V5, V6, V7, Val0, Val1, Val2, Val3, Val4, Val5,
       Val6, Val7, Valid;
  wire [3:0] counter_1_q, multiplexer_6_out;
  wire [12:0] Tag_prime;
  wire [15:0] Address_t;
  wire [31:0] multiplexer_1_out, multiplexer_2_out, multiplexer_3_out, multiplexer_4_out;

  Demultiplexer #(.enable("false")) demultiplexer_1 (
    .out0(demultiplexer_1_out0), .out1(demultiplexer_1_out1), .in(START_q), .sel(Valid));
  D_Flip_Flop START (.clk(Clock), .D(Enable), .Q(START_q));  // open: Qn, preset, en, reset
  and and_1 (str2, decoder_1_out2, selD);
  and and_2 (str0, decoder_1_out0, selD);
  and and_3 (str1, decoder_1_out1, selD);
  Decoder #(.select(2), .enable("false")) decoder_1 (
    .out0(decoder_1_out0), .out1(decoder_1_out1), .out2(decoder_1_out2), .out3(decoder_1_out3),
    .sel(Address[3:2]));
  Demultiplexer #(.enable("false")) demultiplexer_2 (
    .out0(demultiplexer_2_out0), .out1(demultiplexer_2_out1), .in(demultiplexer_1_out1), .sel(eqTag));
  and and_4 (str3, decoder_1_out3, selD);
  or or_1 (L, ChipS1, demultiplexer_1_out0, demultiplexer_2_out0);
  Demultiplexer #(.enable("false")) demultiplexer_3 (.out0(ChipS1), .out1(ChipS2), .in(READ_q), .sel(C__0));
  D_Flip_Flop READ (.clk(Clock), .D(L), .Q(READ_q));  // open: Qn, preset, en, reset
  Multiplexer_part #(.width(32), .enable("false")) multiplexer_1 (
    .in0(RAM_Output_0), .in1({Data[7:0], Data[15:8], Data[23:16], Data[31:24]}), .out(multiplexer_1_out),
    .sel(selD));
  or or_2 (or_2_out, ChipS2, str0);
  Multiplexer_part #(.width(32), .enable("false")) multiplexer_2 (
    .in0(RAM_Output_1), .in1({Data[7:0], Data[15:8], Data[23:16], Data[31:24]}), .out(multiplexer_2_out),
    .sel(selD));
  or or_3 (or_3_out, ChipS2, str1);
  Multiplexer_part #(.width(32), .enable("false")) multiplexer_3 (
    .in0(RAM_Output_2), .in1({Data[7:0], Data[15:8], Data[23:16], Data[31:24]}), .out(multiplexer_3_out),
    .sel(selD));
  or or_4 (or_4_out, ChipS2, str2);
  Multiplexer_part #(.width(32), .enable("false")) multiplexer_4 (
    .in0(RAM_Output_3), .in1({Data[7:0], Data[15:8], Data[23:16], Data[31:24]}), .out(multiplexer_4_out),
    .sel(selD));
  or or_5 (or_5_out, ChipS2, str3);
  or or_6 (or_6_out, ChipS2, demultiplexer_2_out1);
  RAM_part #(.addrWidth(3), .dataWidth(13), .bus("separate")) ram_1 (
    .addr(Address_t[2:0]), .din(Address_t[15:3]), .data(Tag_prime), .str(ChipS2), .clk(Clock), .ld(1'b1),
    .clr(Reset));  // open: sel
  RAM_part #(.addrWidth(3), .dataWidth(32), .bus("separate")) ram_2 (
    .addr(Address_t[2:0]), .din(multiplexer_1_out), .data(Cache_Out_0), .str(or_2_out), .clk(Clock),
    .ld(1'b1), .clr(Reset));  // open: sel
  RAM_part #(.addrWidth(3), .dataWidth(32), .bus("separate")) ram_3 (
    .addr(Address_t[2:0]), .din(multiplexer_2_out), .data(Cache_Out_1), .str(or_3_out), .clk(Clock),
    .ld(1'b1), .clr(Reset));  // open: sel
  RAM_part #(.addrWidth(3), .dataWidth(32), .bus("separate")) ram_4 (
    .addr(Address_t[2:0]), .din(multiplexer_3_out), .data(Cache_Out_2), .str(or_4_out), .clk(Clock),
    .ld(1'b1), .clr(Reset));  // open: sel
  RAM_part #(.addrWidth(3), .dataWidth(32), .bus("separate")) ram_5 (
    .addr(Address_t[2:0]), .din(multiplexer_4_out), .data(Cache_Out_3), .str(or_5_out), .clk(Clock),
    .ld(1'b1), .clr(Reset));  // open: sel
  D_Flip_Flop END (.clk(Clock), .D(or_6_out), .Q(Finish));  // open: Qn, preset, en, reset
  D_Flip_Flop d_ff_1 (.clk(Clock), .D(ChipS2), .Q(Val0), .en(V0), .reset(Reset));  // open: Qn, preset
  D_Flip_Flop d_ff_2 (.clk(Clock), .D(ChipS2), .Q(Val1), .en(V1), .reset(Reset));  // open: Qn, preset
  D_Flip_Flop d_ff_3 (.clk(Clock), .D(ChipS2), .Q(Val2), .en(V2), .reset(Reset));  // open: Qn, preset
  D_Flip_Flop d_ff_4 (.clk(Clock), .D(ChipS2), .Q(Val3), .en(V3), .reset(Reset));  // open: Qn, preset
  D_Flip_Flop d_ff_5 (.clk(Clock), .D(ChipS2), .Q(Val4), .en(V4), .reset(Reset));  // open: Qn, preset
  D_Flip_Flop d_ff_6 (.clk(Clock), .D(ChipS2), .Q(Val5), .en(V5), .reset(Reset));  // open: Qn, preset
  D_Flip_Flop d_ff_7 (.clk(Clock), .D(ChipS2), .Q(Val6), .en(V6), .reset(Reset));  // open: Qn, preset
  D_Flip_Flop d_ff_8 (.clk(Clock), .D(ChipS2), .Q(Val7), .en(V7), .reset(Reset));  // open: Qn, preset
  Multiplexer_part #(.width(16), .enable("false")) multiplexer_5 (
    .in0(Instruction_Address[19:4]), .in1(Address[19:4]), .out(Address_t), .sel(Check));
  and and_5 (selD, Check, Valid, eqTag);
  Counter #(.width(4), .max('hf)) counter_1 (
    .load(L), .D(multiplexer_6_out), .count(ChipS1), .Q(counter_1_q), .clk(Clock));  // open: carry, clr
  Multiplexer_part #(.width(4), .enable("false")) multiplexer_6 (
    .in0(4'b0001), .in1(Read_Time), .out(multiplexer_6_out), .sel(L));
  or or_7 (Chip_Select, ChipS1, ChipS2);
  Decoder #(.select(3), .enable("false")) decoder_2 (
    .out0(decoder_2_out0), .out1(decoder_2_out1), .out2(decoder_2_out2), .out3(decoder_2_out3),
    .out4(decoder_2_out4), .out5(decoder_2_out5), .out6(decoder_2_out6), .out7(decoder_2_out7),
    .sel(Address_t[2:0]));
  Comparator #(.width(4)) comparator_1 (.a(counter_1_q), .b(4'b0000), .eq(C__0));  // open: gt, lt
  Comparator #(.width(13)) comparator_2 (.a(Address_t[15:3]), .b(Tag_prime), .eq(eqTag));  // open: gt, lt
  Multiplexer_part #(.select(3), .enable("false")) multiplexer_7 (
    .in0(Val0), .in1(Val1), .in2(Val2), .in3(Val3), .in4(Val4), .in5(Val5), .in6(Val6), .in7(Val7),
    .out(Valid), .sel(Address_t[2:0]));
  and and_6 (V0, decoder_2_out0, ChipS2);
  and and_7 (V1, decoder_2_out1, ChipS2);
  and and_8 (V2, decoder_2_out2, ChipS2);
  and and_9 (V3, decoder_2_out3, ChipS2);
  and and_10 (V4, decoder_2_out4, ChipS2);
  and and_11 (V5, decoder_2_out5, ChipS2);
  and and_12 (V6, decoder_2_out6, ChipS2);
  and and_13 (V7, decoder_2_out7, ChipS2);

  assign RAM_Address = Instruction_Address[19:4];

  // Other names for the same wires on the sheet: AddressData[15:0] = Address[19:4];
  //   CACHE_OUTPUT_0[31:0] = Cache_Out_0; CACHE_OUTPUT_1[31:0] = Cache_Out_1; CACHE_OUTPUT_2[31:0] = Cache_Out_2;
  //   CACHE_OUTPUT_3[31:0] = Cache_Out_3; chk = Check; clk = Clock; D = ChipS1;
  //   Data_t[31:0] = {Data[7:0], Data[15:8], Data[23:16], Data[31:24]}; en = Enable; Index[2:0] = Address_t[2:0];
  //   AddressPC[15:0] = Instruction_Address[19:4]; rst = Reset; RT[3:0] = Read_Time; Start = L;
  //   Tag[12:0] = Address_t[15:3]; Done = ChipS2; enValid = ChipS2; v = ChipS2

  // Notes on the sheet:
  //   INPUT
  //   CONTROL UNIT 
  //   DIRECT MAPPED 8 LINEAS (INDEX 3 BITS) -> (TAG 13)
  //   TAG
  //   BANK0
  //   BANK1
  //   BANK2
  //   BANK3
  //   VALID
  //   DATA PATH
  //   OUTPUT
endmodule

module Read_RAM (
  input  [31:0] Direction,
  input  Clock,
  input  Reset,
  input  Enable,
  input  [3:0] Read_Time,
  input  [31:0] RAM_Output_0,
  input  [31:0] RAM_Output_1,
  input  [31:0] RAM_Output_2,
  input  [31:0] RAM_Output_3,
  output [15:0] Address,
  output Chip_Select,
  output Done,
  output [31:0] RAM_Output
);

  wire C__0, ChipS1, ChipS2, d_ff_1_q, L;
  wire [3:0] counter_1_q, multiplexer_2_out;
  wire [31:0] multiplexer_1_out;

  Multiplexer_part #(.select(2), .width(32), .enable("false")) multiplexer_1 (
    .in0(RAM_Output_0), .in1(RAM_Output_1), .in2(RAM_Output_2), .in3(RAM_Output_3), .out(multiplexer_1_out),
    .sel(Direction[3:2]));
  Register #(.width(32)) data (
    .D({multiplexer_1_out[7:0], multiplexer_1_out[15:8], multiplexer_1_out[23:16], multiplexer_1_out[31:24]}),
    .en(Chip_Select), .Q(RAM_Output), .clk(Clock), .clr(Reset));
  or or_1 (L, ChipS1, Enable);
  Multiplexer_part #(.width(4), .enable("false")) multiplexer_2 (
    .in0(4'b0001), .in1(Read_Time), .out(multiplexer_2_out), .sel(Enable));
  Demultiplexer #(.enable("false")) demultiplexer_1 (.out0(ChipS1), .out1(ChipS2), .in(d_ff_1_q), .sel(C__0));
  D_Flip_Flop d_ff_1 (.clk(Clock), .D(L), .Q(d_ff_1_q), .reset(Reset));  // open: Qn, preset, en
  Counter #(.width(4), .max('hf)) counter_1 (
    .load(L), .D(multiplexer_2_out), .count(ChipS1), .Q(counter_1_q), .clk(Clock));  // open: carry, clr
  D_Flip_Flop d_ff_2 (.clk(Clock), .D(ChipS2), .Q(Done), .reset(Reset));  // open: Qn, preset, en
  Comparator #(.width(4)) comparator_1 (.a(counter_1_q), .b(4'b0000), .eq(C__0));  // open: gt, lt
  or or_2 (Chip_Select, ChipS1, ChipS2);

  assign Address = Direction[19:4];

  // Other names for the same wires on the sheet: clk = Clock; CS = Chip_Select; D = ChipS1;
  //   Mask[1:0] = Direction[3:2]; en = Enable; rst = Reset; RT[3:0] = Read_Time

  // Notes on the sheet:
  //   CONTROL UNIT 
  //   DATA PATH
endmodule

module Write_RAM (
  input  [31:0] Direction,
  input  Clock,
  input  Reset,
  input  Enable,
  input  [3:0] Write_Time,
  input  [31:0] Data,
  output [3:0] Mask,
  output Chip_Select,
  output Done,
  output [15:0] Address,
  output [31:0] RAM_Output_0,
  output [31:0] RAM_Output_1,
  output [31:0] RAM_Output_2,
  output [31:0] RAM_Output_3
);

  wire C__0, ChipS1, ChipS2, d_ff_1_q, L;
  wire [3:0] counter_1_q, multiplexer_1_out;
  wire [31:0] register_1_q;

  Decoder #(.select(2), .enable("false")) decoder_1 (
    .out0(Mask[0]), .out1(Mask[1]), .out2(Mask[2]), .out3(Mask[3]), .sel(Direction[3:2]));
  Demultiplexer #(.select(2), .width(32), .enable("false")) demultiplexer_1 (
    .out0(RAM_Output_0), .out1(RAM_Output_1), .out2(RAM_Output_2), .out3(RAM_Output_3), .in(register_1_q),
    .sel(Direction[3:2]));
  Register #(.width(32)) register_1 (
    .D({Data[7:0], Data[15:8], Data[23:16], Data[31:24]}), .en(Enable), .Q(register_1_q), .clk(Clock),
    .clr(Reset));
  or or_1 (L, ChipS1, Enable);
  Multiplexer_part #(.width(4), .enable("false")) multiplexer_1 (
    .in0(4'b0001), .in1(Write_Time), .out(multiplexer_1_out), .sel(Enable));
  D_Flip_Flop d_ff_1 (.clk(Clock), .D(L), .Q(d_ff_1_q), .reset(Reset));  // open: Qn, preset, en
  Demultiplexer #(.enable("false")) demultiplexer_2 (.out0(ChipS1), .out1(ChipS2), .in(d_ff_1_q), .sel(C__0));
  Counter #(.width(4), .max('hf)) counter_1 (
    .load(L), .D(multiplexer_1_out), .count(ChipS1), .Q(counter_1_q), .clk(Clock));  // open: carry, clr
  Comparator #(.width(4)) comparator_1 (.a(counter_1_q), .b(4'b0000), .eq(C__0));  // open: gt, lt
  or or_2 (Chip_Select, ChipS1, ChipS2);
  D_Flip_Flop d_ff_2 (.clk(Clock), .D(ChipS2), .Q(Done), .reset(Reset));  // open: Qn, preset, en

  assign Address = Direction[19:4];

  // Other names for the same wires on the sheet: clk = Clock; D = ChipS1; Mask_t[1:0] = Direction[3:2]; en = Enable;
  //   rst = Reset; WT[3:0] = Write_Time

  // Notes on the sheet:
  //   CONTROL UNIT 
  //   DATA PATH
endmodule

module Control_Unit (
  input  nop,
  input  Data_Done,
  input  add,
  input  sub,
  input  Instruction_Done,
  input  mult,
  input  Clock,
  input  mulu,
  input  div,
  input  divu,
  input  addi,
  input  \and ,
  input  \or ,
  input  \nor ,
  input  \xor ,
  input  andi,
  input  ori,
  input  xori,
  input  beq,
  input  bne,
  input  blez,
  input  bgtz,
  input  bltz,
  input  j,
  input  jr,
  input  slt,
  input  sltu,
  input  slti,
  input  sltiu,
  input  lw,
  input  sw,
  input  mfhi,
  input  mflo,
  input  pop,
  input  push,
  input  halt,
  input  tty,
  input  rnd,
  input  kbd,
  output Next,
  output enable_Random,
  output STOP,
  output enable_Read,
  output enable_Write,
  output push_RF,
  output pop_RF,
  output enSP,
  output enable_Instr,
  output enable_TTY,
  output enable_KBD
);

  wire add_prime, addi_prime, and_prime, andi_prime, beq_prime, bgtz_prime, blez_prime, bltz_prime,
       bne_prime, d_ff_1_q, d_ff_1_qn, demultiplexer_1_out0, div_prime, divu_prime, enRd0, enRd1, enWr1,
       j_prime, jr_prime, mfhi_prime, mflo_prime, mult_prime, mulu_prime, NextInst, nop_prime, nor_prime,
       or_2_out, or_4_out, or_prime, ori_prime, slt_prime, slti_prime, sltiu_prime, sltu_prime, sub_prime,
       xor_prime, xori_prime;

  and and_1 (add_prime, NextInst, add);
  and and_2 (divu_prime, NextInst, divu);
  and and_3 (addi_prime, NextInst, addi);
  and and_4 (sltu_prime, NextInst, sltu);
  and and_5 (bne_prime, NextInst, bne);
  and and_6 (mflo_prime, NextInst, mflo);
  and and_7 (enWr1, NextInst, sw);
  and and_8 (enable_KBD, NextInst, kbd);
  or or_1 (enSP, pop_RF, push_RF);
  and and_9 (sub_prime, NextInst, sub);
  and and_10 (and_prime, NextInst, \and );
  and and_11 (andi_prime, NextInst, andi);
  and and_12 (slti_prime, NextInst, slti);
  and and_13 (blez_prime, NextInst, blez);
  and and_14 (enable_Random, NextInst, rnd);
  and and_15 (enRd0, NextInst, pop);
  and and_16 (push_RF, NextInst, push);
  and and_17 (mult_prime, NextInst, mult);
  and and_18 (or_prime, NextInst, \or );
  and and_19 (ori_prime, NextInst, ori);
  and and_20 (sltiu_prime, NextInst, sltiu);
  and and_21 (bgtz_prime, NextInst, bgtz);
  and and_22 (STOP, NextInst, halt);
  and and_23 (pop_RF, Data_Done, pop);
  D_Flip_Flop d_ff_1 (.clk(Clock), .D(or_2_out), .Q(d_ff_1_q), .Qn(d_ff_1_qn), .preset(d_ff_1_qn));  // open: en, reset
  or or_2 (or_2_out, demultiplexer_1_out0, Next);
  or or_3 (enable_Read, enRd0, enRd1);
  and and_24 (mulu_prime, NextInst, mulu);
  and and_25 (nor_prime, NextInst, \nor );
  and and_26 (xori_prime, NextInst, xori);
  and and_27 (jr_prime, NextInst, jr);
  and and_28 (bltz_prime, NextInst, bltz);
  and and_29 (enRd1, NextInst, lw);
  and and_30 (j_prime, NextInst, j);
  Demultiplexer #(.enable("false")) demultiplexer_1 (
    .out0(demultiplexer_1_out0), .out1(enable_Instr), .in(d_ff_1_q), .sel(or_4_out));
  or or_4 (or_4_out, Instruction_Done, Data_Done);
  and and_31 (NextInst, enable_Instr, ~Data_Done);  // AND_Gate
  or or_5 (enable_Write, push_RF, enWr1);
  and and_32 (div_prime, NextInst, div);
  and and_33 (xor_prime, NextInst, \xor );
  and and_34 (slt_prime, NextInst, slt);
  and and_35 (beq_prime, NextInst, beq);
  and and_36 (mfhi_prime, NextInst, mfhi);
  and and_37 (nop_prime, NextInst, nop);
  and and_38 (enable_TTY, NextInst, tty);
  or or_6 (Next, nop_prime, add_prime, sub_prime, mult_prime, mulu_prime, div_prime, divu_prime, and_prime, or_prime, nor_prime, xor_prime, addi_prime, andi_prime, ori_prime, xori_prime, slt_prime, sltu_prime, slti_prime, sltiu_prime, jr_prime, j_prime, beq_prime, bne_prime, blez_prime, bgtz_prime, bltz_prime, mfhi_prime, mflo_prime, STOP, enable_Random, enable_KBD, enable_TTY);

  // Other names for the same wires on the sheet: CLK = Clock; dataDone = Data_Done; enInst = enable_Instr;
  //   enRead = enable_Read; enWrite = enable_Write; halt_prime = STOP; instDone = Instruction_Done;
  //   kbd_prime = enable_KBD; popRF = pop_RF; enWr0 = push_RF; pushRF = push_RF; rnd_prime = enable_Random;
  //   tty_prime = enable_TTY
endmodule

module Data_Path (
  input  Clock,
  input  [6:0] Kbd_ASCII_Data,
  input  [31:0] Cache_Out_0,
  input  [31:0] Cache_Out_1,
  input  Reset,
  input  Kbd_Available,
  input  Next,
  input  enable_Write,
  input  [31:0] RAM_Data,
  input  enable_Random,
  input  push_RF,
  input  [31:0] Cache_Out_2,
  input  [31:0] Cache_Out_3,
  input  enable_Read,
  input  pop_RF,
  input  enable_SP,
  input  Read_Done,
  input  End,
  input  enable_Instr,
  input  Write_Done,
  output Done,
  output Go_Instruction,
  output nop,
  output \and ,
  output beq,
  output slt,
  output add,
  output \or ,
  output bne,
  output sltu,
  output sub,
  output \nor ,
  output blez,
  output slti,
  output mult,
  output \xor ,
  output bgtz,
  output sltiu,
  output Check,
  output mulu,
  output andi,
  output bltz,
  output div,
  output ori,
  output j,
  output lw,
  output divu,
  output xori,
  output jr,
  output sw,
  output addi,
  output mfhi,
  output halt,
  output [31:0] PC,
  output [31:0] Direction,
  output [31:0] Data,
  output mflo,
  output tty,
  output pop,
  output rnd,
  output push,
  output kbd,
  output [6:0] TTY_Data
);

  wire ALU, and_1_out, and_3_out, and_5_out, arithmetic_logic_unit_1_negative_flags,
       arithmetic_logic_unit_1_zero_flags, instruction_decoder_1_unsigned, minus_1, next_t, or_1_out,
       or_2_out, or_3_out, or_5_out, or_8_out, or_10_out, R_W, RAM, RW, SelectK, Zero;
  wire [2:0] SelData;
  wire [3:0] instruction_decoder_1_operation;
  wire [4:0] instruction_decoder_1_destination_address, instruction_decoder_1_selector_a,
       instruction_decoder_1_selector_b;
  wire [31:0] adder_1_out, B, bit_extender_1_out, DI, Hi, instruction_finder_1_instruction, k, Lo,
       multiplexer_1_out, multiplexer_4_out, multiplexer_6_out, Out, program_counter_1_pc_output,
       random_1_random_output, SP;
  wire [31:7] A;

  Multiplexer_part #(.width(32), .enable("false")) multiplexer_1 (
    .in0(k), .in1({A, TTY_Data}), .out(multiplexer_1_out), .sel(jr));
  Branch_Control branch_control_1 (
    .beq(beq), .Instruction_Address(program_counter_1_pc_output), .Next_Instruction_Address(PC),
    .JS(multiplexer_1_out), .bne(bne), .blez(blez), .bgtz(bgtz), .bltz(bltz), .j(j), .jr(jr),
    .ZF(arithmetic_logic_unit_1_zero_flags), .NF(arithmetic_logic_unit_1_negative_flags), .Next(next_t));
  and and_1 (and_1_out, enable_Read, ~Read_Done);  // AND_Gate
  or or_1 (or_1_out, enable_Write, push_RF);
  Program_Counter program_counter_1 (
    .Clock(Clock), .Reset(Reset), .PC_Input(PC), .Next(next_t), .PC_Output(program_counter_1_pc_output));
  or or_2 (or_2_out, enable_Instr, Reset);
  or or_3 (or_3_out, and_1_out, or_1_out);
  and and_2 (Go_Instruction, or_2_out, ~or_3_out);  // AND_Gate
  Instruction_Finder instruction_finder_1 (
    .Clock(Clock), .Direction(program_counter_1_pc_output), .Reset(Reset), .Enable(End),
    .RAM_Output_0(Cache_Out_0), .RAM_Output_1(Cache_Out_1), .RAM_Output_2(Cache_Out_2),
    .RAM_Output_3(Cache_Out_3), .Instruction(instruction_finder_1_instruction), .Done(Done));
  or or_4 (next_t, Next, Read_Done, Write_Done);
  or or_5 (or_5_out, Read_Done, Write_Done);
  and and_3 (and_3_out, or_5_out, lw);
  or or_6 (R_W, and_3_out, RW, pop_RF);
  Random random_1 (.Clock(Clock), .Enable(enable_Random), .Random_Output(random_1_random_output));
  or or_7 (ALU, add, sub, mult, mulu, div, divu, addi, \and , \or , \nor , \xor , andi, ori, xori, slt, sltu, slti, sltiu);
  Instruction_Decoder instruction_decoder_1 (
    .Destination_Address(instruction_decoder_1_destination_address), .R_W(RW),
    .Selector_A(instruction_decoder_1_selector_a), .Selector_B(instruction_decoder_1_selector_b), .k(k),
    .Operation(instruction_decoder_1_operation), .Instruction(instruction_finder_1_instruction),
    .unSigned(instruction_decoder_1_unsigned), .nop(nop), .add(add), .sub(sub), .mult(mult), .mulu(mulu),
    .div(div), .divu(divu), .addi(addi), .\and (\and ), .\or (\or ), .\nor (\nor ), .\xor (\xor ),
    .andi(andi), .ori(ori), .xori(xori), .beq(beq), .bne(bne), .blez(blez), .bgtz(bgtz), .bltz(bltz), .j(j),
    .jr(jr), .slt(slt), .sltu(sltu), .slti(slti), .sltiu(sltiu), .lw(lw), .sw(sw), .mfhi(mfhi), .mflo(mflo),
    .pop(pop), .push(push), .halt(halt), .tty(tty), .rnd(rnd), .kbd(kbd), .Next(Next));
  assign bit_extender_1_out = {{25{1'b0}}, Kbd_ASCII_Data};  // Bit_Extender bit_extender_1
  Multiplexer_part #(.select(3), .width(32), .enable("false")) multiplexer_2 (
    .in0(Out), .in1(random_1_random_output), .in2(Lo), .in3(Hi), .in4(RAM_Data), .in5(bit_extender_1_out),
    .in6({32{1'b1}}), .out(DI), .sel(SelData));  // open: in7
  Adder #(.width(32)) adder_1 (.a({A, TTY_Data}), .b(k), .out(adder_1_out));  // open: cin, cout
  Multiplexer_part #(.width(32), .enable("false")) multiplexer_3 (
    .in0(adder_1_out), .in1(SP), .out(Direction), .sel(or_8_out));
  or or_8 (or_8_out, pop, push);
  Register_File register_file_1 (
    .Data_Input(DI), .Clock(Clock), .Reset(Reset), .Output_A({A, TTY_Data}), .Output_B(B), .R_W(R_W),
    .Destination_Address(instruction_decoder_1_destination_address),
    .Selector_A(instruction_decoder_1_selector_a), .Selector_B(instruction_decoder_1_selector_b),
    .Pop(pop_RF), .Push(push_RF), .Stack_Pointer(SP), .enSP(enable_SP));
  Priority_Encoder priority_encoder_1 (
    .in0(ALU), .in1(rnd), .in2(mflo), .in3(mfhi), .in4(RAM), .in5(kbd), .in6(minus_1), .out(SelData));  // open: in7, en_in, gs, en_out
  or or_9 (SelectK, addi, slti, sltiu, andi, ori, xori);
  Multiplexer_part #(.width(32), .enable("false")) multiplexer_4 (
    .in0(B), .in1(k), .out(multiplexer_4_out), .sel(SelectK));
  or or_10 (or_10_out, push, sw);
  Multiplexer_part #(.width(32), .enable("false")) multiplexer_5 (.in0(B), .in1({A, TTY_Data}), .out(Data), .sel(push));
  Arithmetic_Logic_Unit arithmetic_logic_unit_1 (
    .A({A, TTY_Data}), .B(multiplexer_6_out), .Lo(Lo), .Operation(instruction_decoder_1_operation),
    .Output(Out), .Zero_Flags(arithmetic_logic_unit_1_zero_flags),
    .Negative_Flags(arithmetic_logic_unit_1_negative_flags), .Hi(Hi),
    .unSigned(instruction_decoder_1_unsigned), .Clock(Clock), .Reset(Reset));
  Multiplexer_part #(.width(32), .enable("false")) multiplexer_6 (
    .in0(multiplexer_4_out), .in1({32{1'b0}}), .out(multiplexer_6_out), .sel(Zero));
  or or_11 (Zero, blez, bltz, bgtz);
  and and_4 (minus_1, ~Kbd_Available, kbd);  // AND_Gate
  or or_12 (RAM, pop, lw);
  D_Flip_Flop d_ff_1 (.clk(Clock), .D(and_5_out), .Q(Check), .reset(Reset));  // open: Qn, preset, en
  and and_5 (and_5_out, or_10_out, enable_Write);

  // Other names for the same wires on the sheet: A[6:0] = TTY_Data; clk = Clock; enInst = enable_Instr;
  //   enRead = enable_Read; enRnd = enable_Random; enSP = enable_SP; enWrite = enable_Write;
  //   KBD_AVAIL = Kbd_Available; KBD_DATA[6:0] = Kbd_ASCII_Data; popRF = pop_RF; pushRF = push_RF; ReadD = Read_Done;
  //   rst = Reset; WriteD = Write_Done
endmodule

module Branch_Control (
  input  beq,
  input  bne,
  input  blez,
  input  bgtz,
  input  bltz,
  input  Next,
  input  j,
  input  ZF,
  input  jr,
  input  NF,
  input  [31:0] JS,
  input  [31:0] Instruction_Address,
  output [31:0] Next_Instruction_Address
);

  wire and_1_out, and_2_out, and_3_out, and_4_out, and_5_out, jumpEn, or_1_out, or_2_out, or_3_out;
  wire [31:0] Branch, multiplexer_1_out, multiplexer_2_out, PC_4;

  Adder #(.width(32)) adder_1 (.a(Instruction_Address), .b(32'h4), .out(PC_4));  // open: cin, cout
  Adder #(.width(32)) adder_2 (.a(PC_4), .b(JS), .out(Branch));  // open: cin, cout
  and and_1 (and_1_out, beq, ZF);
  and and_2 (and_2_out, ~ZF, bne);  // AND_Gate
  and and_3 (and_3_out, blez, or_1_out);
  or or_1 (or_1_out, ZF, NF);
  and and_4 (and_4_out, bgtz, ~or_2_out);  // AND_Gate
  or or_2 (or_2_out, ZF, NF);
  and and_5 (and_5_out, bltz, NF);
  or or_3 (or_3_out, and_1_out, and_2_out, and_3_out, and_4_out, and_5_out);
  Multiplexer_part #(.width(32), .enable("false")) multiplexer_1 (
    .in0(PC_4), .in1(multiplexer_2_out), .out(multiplexer_1_out), .sel(jumpEn));
  Multiplexer_part #(.select(2), .width(32), .enable("false")) multiplexer_2 (
    .in0(Branch), .in1(JS), .in2({Instruction_Address[31:28], JS[27:0]}), .out(multiplexer_2_out),
    .sel({j, jr}));  // open: in3
  or or_4 (jumpEn, or_3_out, j, jr);
  Multiplexer_part #(.width(32), .enable("false")) multiplexer_3 (
    .in0(Instruction_Address), .in1(multiplexer_1_out), .out(Next_Instruction_Address), .sel(Next));

  // Other names for the same wires on the sheet: IA[31:0] = Instruction_Address;
  //   IA_prime[31:0] = Next_Instruction_Address; jumpK[31:0] = {Instruction_Address[31:28], JS[27:0]}; nt = Next;
  //   Selector[1:0] = {j, jr}
endmodule

module Program_Counter (
  input  Clock,
  input  Reset,
  input  [31:0] PC_Input,
  input  Next,
  output [31:0] PC_Output
);

  Register #(.width(32)) register_1 (.D(PC_Input), .en(Next), .Q(PC_Output), .clk(Clock), .clr(Reset));

  // Other names for the same wires on the sheet: clk = Clock; nt = Next; rst = Reset
endmodule

module Instruction_Finder (
  input  [31:0] Direction,
  input  Clock,
  input  Reset,
  input  Enable,
  input  [31:0] RAM_Output_0,
  input  [31:0] RAM_Output_1,
  input  [31:0] RAM_Output_2,
  input  [31:0] RAM_Output_3,
  output Done,
  output [31:0] Instruction
);

  wire [31:0] multiplexer_1_out;

  Multiplexer_part #(.select(2), .width(32), .enable("false")) multiplexer_1 (
    .in0(RAM_Output_0), .in1(RAM_Output_1), .in2(RAM_Output_2), .in3(RAM_Output_3), .out(multiplexer_1_out),
    .sel(Direction[3:2]));
  Register #(.width(32)) inst (
    .D({multiplexer_1_out[7:0], multiplexer_1_out[15:8], multiplexer_1_out[23:16], multiplexer_1_out[31:24]}),
    .en(Enable), .Q(Instruction), .clk(Clock), .clr(Reset));
  D_Flip_Flop d_ff_1 (.clk(Clock), .D(Enable), .Q(Done), .reset(Reset));  // open: Qn, preset, en

  // Other names for the same wires on the sheet: clk = Clock; Mask[1:0] = Direction[3:2]; en = Enable; rst = Reset
endmodule

module Instruction_Decoder (
  input  [31:0] Instruction,
  input  Next,
  output nop,
  output slt,
  output add,
  output sltu,
  output sub,
  output slti,
  output mult,
  output sltiu,
  output mulu,
  output div,
  output lw,
  output [4:0] Destination_Address,
  output divu,
  output sw,
  output addi,
  output mfhi,
  output R_W,
  output \and ,
  output mflo,
  output \or ,
  output pop,
  output \nor ,
  output push,
  output [4:0] Selector_A,
  output \xor ,
  output andi,
  output halt,
  output [4:0] Selector_B,
  output ori,
  output tty,
  output xori,
  output rnd,
  output kbd,
  output beq,
  output [31:0] k,
  output bne,
  output blez,
  output bgtz,
  output bltz,
  output [3:0] Operation,
  output j,
  output jr,
  output unSigned
);

  wire or_2_out, or_4_out, or_5_out, or_6_out, or_7_out, or_8_out, or_9_out, or_10_out, or_11_out, or_12_out,
       or_13_out, or_14_out, priority_encoder_1_en_out, priority_encoder_2_en_out, St;
  wire [1:0] multiplexer_2_out, priority_encoder_1_out;
  wire [2:0] priority_encoder_2_out;

  Multiplexer_part #(.width(5), .enable("false")) multiplexer_1 (
    .in0(Instruction[15:11]), .in1(Instruction[20:16]), .out(Destination_Address), .sel(St));
  or or_1 (Operation[3], slt, sltu, slti, sltiu);
  or or_2 (or_2_out, mulu, divu, sltu, sltiu);
  or or_3 (St, addi, slti, sltiu, andi, ori, xori, lw);
  and and_1 (unSigned, or_2_out, Next);
  or or_4 (or_4_out, kbd, add, sub, mult, mulu, div, divu, slt, sltu, \and , \or , \nor , \xor , addi, slti, sltiu, andi, ori, xori, mfhi, mflo, rnd);
  or or_5 (or_5_out, addi, slti, sltiu, lw, sw);
  or or_6 (or_6_out, andi, ori, xori);
  or or_7 (or_7_out, beq, bne, blez, bgtz, bltz);
  and and_2 (R_W, or_4_out, Next);
  Instruction_R_Type instruction_r_type_1 (
    .Op_Code(Instruction[31:26]), .Func_Code(Instruction[5:0]), .nop(nop), .add(add), .sub(sub), .mult(mult),
    .mulu(mulu), .div(div), .divu(divu), .slt(slt), .\and (\and ), .\xor (\xor ), .pop(pop), .jr(jr),
    .mfhi(mfhi), .mflo(mflo), .halt(halt), .tty(tty), .rnd(rnd), .kbd(kbd), .sltu(sltu), .\or (\or ),
    .\nor (\nor ), .push(push));
  Instruction_J_Type instruction_j_type_1 (.Op_Code(Instruction[31:26]), .j(j));
  Priority_Encoder #(.select(2)) priority_encoder_1 (
    .in0(or_5_out), .in1(or_6_out), .in2(or_7_out), .in3(j), .out(priority_encoder_1_out),
    .en_out(priority_encoder_1_en_out));  // open: gs, en_in
  Multiplexer_part #(.width(2), .enable("false")) multiplexer_2 (
    .in0(priority_encoder_1_out), .in1(2'b00), .out(multiplexer_2_out), .sel(priority_encoder_1_en_out));
  or or_8 (or_8_out, add, addi, blez, bgtz, bltz);
  or or_9 (or_9_out, sub, beq, bne);
  or or_10 (or_10_out, mult, mulu);
  or or_11 (or_11_out, div, divu);
  or or_12 (or_12_out, \and , andi);
  or or_13 (or_13_out, \or , ori);
  or or_14 (or_14_out, \xor , xori);
  Multiplexer_part #(.select(2), .width(32), .enable("false")) multiplexer_3 (
    .in0({{17{Instruction[15]}}, Instruction[14:0]}), .in1({{16{1'b0}}, Instruction[15:0]}),
    .in2({{15{Instruction[15]}}, Instruction[14:0], 2'b00}), .in3({4'b0000, Instruction[25:0], 2'b00}),
    .out(k), .sel(multiplexer_2_out));
  Priority_Encoder priority_encoder_2 (
    .in0(or_8_out), .in1(or_9_out), .in2(or_10_out), .in3(or_11_out), .in4(or_12_out), .in5(or_13_out),
    .in6(\nor ), .in7(or_14_out), .out(priority_encoder_2_out), .en_out(priority_encoder_2_en_out));  // open: en_in, gs
  Multiplexer_part #(.width(3), .enable("false")) multiplexer_4 (
    .in0(priority_encoder_2_out), .in1(3'b000), .out(Operation[2:0]), .sel(priority_encoder_2_en_out));
  Instruction_I_Type instruction_i_type_1 (
    .Op_Code(Instruction[31:26]), .addi(addi), .slti(slti), .sltiu(sltiu), .andi(andi), .ori(ori),
    .xori(xori), .lw(lw), .sw(sw), .beq(beq), .bne(bne), .blez(blez), .bgtz(bgtz), .bltz(bltz));

  assign Selector_A = Instruction[25:21];
  assign Selector_B = Instruction[20:16];

  // Other names for the same wires on the sheet: Constant[15:0] = Instruction[15:0];
  //   Destiny[25:0] = Instruction[25:0]; Func_Code[5:0] = Instruction[5:0];
  //   Offset1[31:0] = {{17{Instruction[15]}}, Instruction[14:0]}; Offset2[15:0] = Instruction[15:0];
  //   Offset3[31:2] = {{15{Instruction[15]}}, Instruction[14:0]}; Offset4[27:2] = Instruction[25:0];
  //   x[4:0] = Instruction[10:6]; Rd[4:0] = Instruction[15:11]; Op_Code[5:0] = Instruction[31:26];
  //   Op[2:0] = Operation[2:0]; enSlt = Operation[3]; Rs[4:0] = Instruction[25:21]; Rt[4:0] = Instruction[20:16]

  // Notes on the sheet:
  //   J
  //   I
  //   R
endmodule

module Instruction_R_Type (
  input  [5:0] Op_Code,
  input  [5:0] Func_Code,
  output nop,
  output add,
  output sub,
  output mult,
  output mulu,
  output div,
  output divu,
  output slt,
  output sltu,
  output \and ,
  output \or ,
  output \nor ,
  output \xor ,
  output pop,
  output push,
  output jr,
  output mfhi,
  output mflo,
  output halt,
  output tty,
  output rnd,
  output kbd
);

  wire en1, en2, en3;

  and and_1 (en1, ~Op_Code[0], ~Op_Code[1], ~Op_Code[2], ~Op_Code[3], ~Op_Code[4], ~Op_Code[5]);  // AND_Gate
  and and_2 (en2, Op_Code[0], Op_Code[1], Op_Code[2], Op_Code[3], Op_Code[4], Op_Code[5]);
  and and_3 (en3, ~Op_Code[0], ~Op_Code[1], ~Op_Code[2], Op_Code[3], Op_Code[4], Op_Code[5]);  // AND_Gate
  and and_4 (nop, en1, ~Func_Code[0], ~Func_Code[1], ~Func_Code[2], ~Func_Code[3], ~Func_Code[4], ~Func_Code[5]);  // AND_Gate
  and and_5 (mulu, en1, Func_Code[0], ~Func_Code[1], ~Func_Code[2], Func_Code[3], Func_Code[4], ~Func_Code[5]);  // AND_Gate
  and and_6 (sltu, en1, Func_Code[0], Func_Code[1], ~Func_Code[2], Func_Code[3], ~Func_Code[4], Func_Code[5]);  // AND_Gate
  and and_7 (\xor , en1, ~Func_Code[0], ~Func_Code[1], ~Func_Code[2], Func_Code[3], ~Func_Code[4], Func_Code[5]);  // AND_Gate
  and and_8 (mfhi, en1, ~Func_Code[0], ~Func_Code[1], ~Func_Code[2], ~Func_Code[3], Func_Code[4], ~Func_Code[5]);  // AND_Gate
  and and_9 (rnd, en2, ~Func_Code[0], Func_Code[1], ~Func_Code[2], ~Func_Code[3], ~Func_Code[4], ~Func_Code[5]);  // AND_Gate
  and and_10 (add, en1, ~Func_Code[0], ~Func_Code[1], ~Func_Code[2], ~Func_Code[3], ~Func_Code[4], Func_Code[5]);  // AND_Gate
  and and_11 (div, en1, ~Func_Code[0], Func_Code[1], ~Func_Code[2], Func_Code[3], Func_Code[4], ~Func_Code[5]);  // AND_Gate
  and and_12 (\and , en1, ~Func_Code[0], ~Func_Code[1], Func_Code[2], ~Func_Code[3], ~Func_Code[4], Func_Code[5]);  // AND_Gate
  and and_13 (pop, en3, ~Func_Code[0], ~Func_Code[1], ~Func_Code[2], ~Func_Code[3], ~Func_Code[4], ~Func_Code[5]);  // AND_Gate
  and and_14 (mflo, en1, ~Func_Code[0], Func_Code[1], ~Func_Code[2], ~Func_Code[3], Func_Code[4], ~Func_Code[5]);  // AND_Gate
  and and_15 (kbd, en2, ~Func_Code[0], ~Func_Code[1], Func_Code[2], ~Func_Code[3], ~Func_Code[4], ~Func_Code[5]);  // AND_Gate
  and and_16 (sub, en1, ~Func_Code[0], Func_Code[1], ~Func_Code[2], ~Func_Code[3], ~Func_Code[4], Func_Code[5]);  // AND_Gate
  and and_17 (divu, en1, Func_Code[0], Func_Code[1], ~Func_Code[2], Func_Code[3], Func_Code[4], ~Func_Code[5]);  // AND_Gate
  and and_18 (\or , en1, Func_Code[0], ~Func_Code[1], Func_Code[2], ~Func_Code[3], ~Func_Code[4], Func_Code[5]);  // AND_Gate
  and and_19 (push, en3, Func_Code[0], ~Func_Code[1], ~Func_Code[2], ~Func_Code[3], ~Func_Code[4], ~Func_Code[5]);  // AND_Gate
  and and_20 (halt, en2, Func_Code[0], Func_Code[1], Func_Code[2], Func_Code[3], Func_Code[4], Func_Code[5]);
  and and_21 (mult, en1, ~Func_Code[0], ~Func_Code[1], ~Func_Code[2], Func_Code[3], Func_Code[4], ~Func_Code[5]);  // AND_Gate
  and and_22 (slt, en1, ~Func_Code[0], Func_Code[1], ~Func_Code[2], Func_Code[3], ~Func_Code[4], Func_Code[5]);  // AND_Gate
  and and_23 (\nor , en1, Func_Code[0], Func_Code[1], Func_Code[2], ~Func_Code[3], ~Func_Code[4], Func_Code[5]);  // AND_Gate
  and and_24 (jr, en1, ~Func_Code[0], ~Func_Code[1], ~Func_Code[2], Func_Code[3], ~Func_Code[4], ~Func_Code[5]);  // AND_Gate
  and and_25 (tty, en2, Func_Code[0], ~Func_Code[1], ~Func_Code[2], ~Func_Code[3], ~Func_Code[4], ~Func_Code[5]);  // AND_Gate

  // Notes on the sheet:
  //   NOP
  //   MULU
  //   SLTU
  //   XOR
  //   MFHI
  //   RND
  //   ADD
  //   DIV
  //   AND
  //   POP
  //   MFLO
  //   KBD
  //   SUB
  //   DIVU
  //   OR
  //   PUSH
  //   HALT
  //   MULT
  //   SLT
  //   NOR
  //   JR
  //   TTY
endmodule

module Instruction_I_Type (
  input  [5:0] Op_Code,
  output addi,
  output slti,
  output sltiu,
  output andi,
  output ori,
  output xori,
  output lw,
  output sw,
  output beq,
  output bne,
  output blez,
  output bgtz,
  output bltz
);

  and and_1 (addi, ~Op_Code[0], ~Op_Code[1], ~Op_Code[2], Op_Code[3], ~Op_Code[4], ~Op_Code[5]);  // AND_Gate
  and and_2 (ori, Op_Code[0], ~Op_Code[1], Op_Code[2], Op_Code[3], ~Op_Code[4], ~Op_Code[5]);  // AND_Gate
  and and_3 (beq, ~Op_Code[0], ~Op_Code[1], Op_Code[2], ~Op_Code[3], ~Op_Code[4], ~Op_Code[5]);  // AND_Gate
  and and_4 (bltz, Op_Code[0], ~Op_Code[1], ~Op_Code[2], ~Op_Code[3], ~Op_Code[4], ~Op_Code[5]);  // AND_Gate
  and and_5 (slti, ~Op_Code[0], Op_Code[1], ~Op_Code[2], Op_Code[3], ~Op_Code[4], ~Op_Code[5]);  // AND_Gate
  and and_6 (xori, ~Op_Code[0], Op_Code[1], Op_Code[2], Op_Code[3], ~Op_Code[4], ~Op_Code[5]);  // AND_Gate
  and and_7 (bne, Op_Code[0], ~Op_Code[1], Op_Code[2], ~Op_Code[3], ~Op_Code[4], ~Op_Code[5]);  // AND_Gate
  and and_8 (sltiu, Op_Code[0], Op_Code[1], ~Op_Code[2], Op_Code[3], ~Op_Code[4], ~Op_Code[5]);  // AND_Gate
  and and_9 (lw, Op_Code[0], Op_Code[1], ~Op_Code[2], ~Op_Code[3], ~Op_Code[4], Op_Code[5]);  // AND_Gate
  and and_10 (blez, ~Op_Code[0], Op_Code[1], Op_Code[2], ~Op_Code[3], ~Op_Code[4], ~Op_Code[5]);  // AND_Gate
  and and_11 (andi, ~Op_Code[0], ~Op_Code[1], Op_Code[2], Op_Code[3], ~Op_Code[4], ~Op_Code[5]);  // AND_Gate
  and and_12 (sw, Op_Code[0], Op_Code[1], ~Op_Code[2], Op_Code[3], ~Op_Code[4], Op_Code[5]);  // AND_Gate
  and and_13 (bgtz, Op_Code[0], Op_Code[1], Op_Code[2], ~Op_Code[3], ~Op_Code[4], ~Op_Code[5]);  // AND_Gate

  // Notes on the sheet:
  //   ADDI
  //   ORI
  //   BEQ
  //   BLTZ
  //   SLTI
  //   XORI
  //   BNE
  //   SLTIU
  //   LW
  //   BLEZ
  //   ANDI
  //   SW
  //   BGTZ
endmodule

module Instruction_J_Type (
  input  [5:0] Op_Code,
  output j
);

  and and_1 (j, ~Op_Code[0], Op_Code[1], ~Op_Code[2], ~Op_Code[3], ~Op_Code[4], ~Op_Code[5]);  // AND_Gate

  // Notes on the sheet:
  //   J
endmodule

module Register_File (
  input  R_W,
  input  [4:0] Selector_A,
  input  [4:0] Destination_Address,
  input  [31:0] Data_Input,
  input  Clock,
  input  Reset,
  input  Pop,
  input  enSP,
  input  Push,
  input  [4:0] Selector_B,
  output [31:0] Output_A,
  output [31:0] Output_B,
  output [31:0] Stack_Pointer
);

  wire and_1_out, enPP, L00, L01, L02, L03, L04, L05, L06, L07, L08, L09, L10, L11, L12, L13, L14, L15, L16,
       L17, L18, L19, L20, L21, L22, L23, L24, L25, L26, L27, L28, L29, L30, L31, LSP;
  wire [31:0] adder_1_out, multiplexer_1_out, Q00, Q01, Q02, Q03, Q04, Q05, Q06, Q07, Q08, Q09, Q10, Q11,
       Q12, Q13, Q14, Q15, Q16, Q17, Q18, Q19, Q20, Q21, Q22, Q23, Q24, Q25, Q26, Q27, Q28, Q29, Q30, SP,
       subtractor_1_out;

  Demultiplexer #(.select(5), .enable("false")) demultiplexer_1 (
    .out0(L00), .out1(L01), .out2(L02), .out3(L03), .out4(L04), .out5(L05), .out6(L06), .out7(L07),
    .out8(L08), .out9(L09), .out10(L10), .out11(L11), .out12(L12), .out13(L13), .out14(L14), .out15(L15),
    .out16(L16), .out17(L17), .out18(L18), .out19(L19), .out20(L20), .out21(L21), .out22(L22), .out23(L23),
    .out24(L24), .out25(L25), .out26(L26), .out27(L27), .out28(L28), .out29(L29), .out30(L30), .out31(L31),
    .in(R_W), .sel(Destination_Address));
  or or_1 (LSP, enSP, L31);
  or or_2 (enPP, Pop, Push);
  Subtractor #(.width(32)) subtractor_1 (.a(Stack_Pointer), .b(32'h4), .out(subtractor_1_out));  // open: bin, bout
  Multiplexer_part #(.width(32)) multiplexer_1 (
    .in0(subtractor_1_out), .in1(adder_1_out), .out(multiplexer_1_out), .sel(Pop), .en(enPP));
  Adder #(.width(32)) adder_1 (.a(Stack_Pointer), .b(32'h4), .out(adder_1_out));  // open: cin, cout
  Multiplexer_part #(.width(32), .enable("false")) multiplexer_2 (
    .in0(Data_Input), .in1(multiplexer_1_out), .out(SP), .sel(enPP));
  and and_1 (and_1_out, L00, ~L00);  // AND_Gate
  Register #(.width(32)) register_1 (.D(Data_Input), .en(and_1_out), .Q(Q00), .clk(Clock), .clr(Reset));
  Register #(.width(32)) register_2 (.D(Data_Input), .en(L04), .Q(Q04), .clk(Clock), .clr(Reset));
  Register #(.width(32)) register_3 (.D(Data_Input), .en(L08), .Q(Q08), .clk(Clock), .clr(Reset));
  Register #(.width(32)) register_4 (.D(Data_Input), .en(L12), .Q(Q12), .clk(Clock), .clr(Reset));
  Register #(.width(32)) register_5 (.D(Data_Input), .en(L16), .Q(Q16), .clk(Clock), .clr(Reset));
  Register #(.width(32)) register_6 (.D(Data_Input), .en(L20), .Q(Q20), .clk(Clock), .clr(Reset));
  Register #(.width(32)) register_7 (.D(Data_Input), .en(L24), .Q(Q24), .clk(Clock), .clr(Reset));
  Register #(.width(32)) register_8 (.D(Data_Input), .en(L28), .Q(Q28), .clk(Clock), .clr(Reset));
  Register #(.width(32)) register_9 (.D(Data_Input), .en(L01), .Q(Q01), .clk(Clock), .clr(Reset));
  Register #(.width(32)) register_10 (.D(Data_Input), .en(L05), .Q(Q05), .clk(Clock), .clr(Reset));
  Register #(.width(32)) register_11 (.D(Data_Input), .en(L09), .Q(Q09), .clk(Clock), .clr(Reset));
  Register #(.width(32)) register_12 (.D(Data_Input), .en(L13), .Q(Q13), .clk(Clock), .clr(Reset));
  Register #(.width(32)) register_13 (.D(Data_Input), .en(L17), .Q(Q17), .clk(Clock), .clr(Reset));
  Register #(.width(32)) register_14 (.D(Data_Input), .en(L21), .Q(Q21), .clk(Clock), .clr(Reset));
  Register #(.width(32)) register_15 (.D(Data_Input), .en(L25), .Q(Q25), .clk(Clock), .clr(Reset));
  Register #(.width(32)) register_16 (.D(Data_Input), .en(L29), .Q(Q29), .clk(Clock), .clr(Reset));
  Register #(.width(32)) register_17 (.D(Data_Input), .en(L02), .Q(Q02), .clk(Clock), .clr(Reset));
  Register #(.width(32)) register_18 (.D(Data_Input), .en(L06), .Q(Q06), .clk(Clock), .clr(Reset));
  Register #(.width(32)) register_19 (.D(Data_Input), .en(L10), .Q(Q10), .clk(Clock), .clr(Reset));
  Register #(.width(32)) register_20 (.D(Data_Input), .en(L14), .Q(Q14), .clk(Clock), .clr(Reset));
  Register #(.width(32)) register_21 (.D(Data_Input), .en(L18), .Q(Q18), .clk(Clock), .clr(Reset));
  Register #(.width(32)) register_22 (.D(Data_Input), .en(L22), .Q(Q22), .clk(Clock), .clr(Reset));
  Register #(.width(32)) register_23 (.D(Data_Input), .en(L26), .Q(Q26), .clk(Clock), .clr(Reset));
  Register #(.width(32)) register_24 (.D(Data_Input), .en(L30), .Q(Q30), .clk(Clock), .clr(Reset));
  Register #(.width(32)) register_25 (.D(Data_Input), .en(L03), .Q(Q03), .clk(Clock), .clr(Reset));
  Register #(.width(32)) register_26 (.D(Data_Input), .en(L07), .Q(Q07), .clk(Clock), .clr(Reset));
  Register #(.width(32)) register_27 (.D(Data_Input), .en(L11), .Q(Q11), .clk(Clock), .clr(Reset));
  Register #(.width(32)) register_28 (.D(Data_Input), .en(L15), .Q(Q15), .clk(Clock), .clr(Reset));
  Register #(.width(32)) register_29 (.D(Data_Input), .en(L19), .Q(Q19), .clk(Clock), .clr(Reset));
  Register #(.width(32)) register_30 (.D(Data_Input), .en(L23), .Q(Q23), .clk(Clock), .clr(Reset));
  Register #(.width(32)) register_31 (.D(Data_Input), .en(L27), .Q(Q27), .clk(Clock), .clr(Reset));
  Register #(.width(32)) register_32 (.D(SP), .en(LSP), .Q(Stack_Pointer), .clk(Clock), .clr(Reset));
  Multiplexer multiplexer_3 (
    .I00(Q00), .I01(Q01), .I02(Q02), .I03(Q03), .I04(Q04), .I05(Q05), .I06(Q06), .I07(Q07), .I08(Q08),
    .I09(Q09), .I10(Q10), .I11(Q11), .I12(Q12), .I13(Q13), .I14(Q14), .I15(Q15), .I16(Q16), .I17(Q17),
    .I18(Q18), .I19(Q19), .I20(Q20), .I21(Q21), .I22(Q22), .I23(Q23), .I24(Q24), .I25(Q25), .I26(Q26),
    .I27(Q27), .I28(Q28), .I29(Q29), .I30(Q30), .I31(Stack_Pointer), .Output(Output_A), .Selector(Selector_A));
  Multiplexer multiplexer_4 (
    .I00(Q00), .I01(Q01), .I02(Q02), .I03(Q03), .I04(Q04), .I05(Q05), .I06(Q06), .I07(Q07), .I08(Q08),
    .I09(Q09), .I10(Q10), .I11(Q11), .I12(Q12), .I13(Q13), .I14(Q14), .I15(Q15), .I16(Q16), .I17(Q17),
    .I18(Q18), .I19(Q19), .I20(Q20), .I21(Q21), .I22(Q22), .I23(Q23), .I24(Q24), .I25(Q25), .I26(Q26),
    .I27(Q27), .I28(Q28), .I29(Q29), .I30(Q30), .I31(Stack_Pointer), .Output(Output_B), .Selector(Selector_B));

  // Other names for the same wires on the sheet: clk = Clock; DI[31:0] = Data_Input; OA[31:0] = Output_A;
  //   OB[31:0] = Output_B; Q31[31:0] = Stack_Pointer; rst = Reset

  // Notes on the sheet:
  //   Constante 0
  //   Stack Pointer
endmodule

module Arithmetic_Logic_Unit (
  input  [31:0] A,
  input  [31:0] B,
  input  [3:0] Operation,
  input  unSigned,
  input  Clock,
  input  Reset,
  output Zero_Flags,
  output Negative_Flags,
  output [31:0] Output,
  output [31:0] Hi,
  output [31:0] Lo
);

  wire and_2_out, and_4_out, and_5_out, and_6_out, comparator_1_lt, comparator_2_lt, div, L, nor_2_out,
       not_1_out, not_2_out, not_3_out, not_4_out, xor_2_out;
  wire [31:0] A_prime, adder_1_out, and_3_out, B_prime, divider_1_out, Hi_star, Hi_t, Lo_star, Lo_t,
       multiplexer_1_out, multiplexer_2_out, multiplexer_3_out, multiplexer_4_out, multiplexer_5_out,
       multiplexer_7_out, multiplexer_8_out, multiplier_1_cout, multiplier_1_out, mulu_1_hi, mulu_1_lo,
       negator_3_out, nor_1_out, or_2_out, subtractor_1_out, xor_1_out;

  Multiplexer_part #(.width(32), .enable("false")) multiplexer_1 (
    .in0(Hi_star), .in1(Hi_t), .out(multiplexer_1_out), .sel(div));
  Register #(.width(32)) register_1 (.D(multiplexer_1_out), .en(L), .Q(Hi), .clk(Clock), .clr(Reset));
  Multiplexer_part #(.width(32), .enable("false")) multiplexer_2 (
    .in0(Lo_star), .in1(Lo_t), .out(multiplexer_2_out), .sel(div));
  Register #(.width(32)) register_2 (.D(multiplexer_2_out), .en(L), .Q(Lo), .clk(Clock), .clr(Reset));
  and and_1 (div, Operation[0], Operation[1], ~Operation[2], ~Operation[3]);  // AND_Gate
  or or_1 (L, div, and_2_out);
  and and_2 (and_2_out, ~Operation[0], Operation[1], ~Operation[2], ~Operation[3]);  // AND_Gate
  Comparator #(.width(32)) comparator_1 (.a(A), .b(B), .lt(comparator_1_lt));  // open: gt, eq
  Comparator #(.width(32), .mode("unsigned")) comparator_2 (.a(A), .b(B), .lt(comparator_2_lt));  // open: gt, eq
  Adder #(.width(32)) adder_1 (.a(A), .b(B), .out(adder_1_out));  // open: cin, cout
  Subtractor #(.width(32)) subtractor_1 (.a(A), .b(B), .out(subtractor_1_out));  // open: bin, bout
  assign and_3_out = A & B;  // AND_Gate and_3, 32 bits wide
  assign or_2_out = A | B;  // OR_Gate or_2, 32 bits wide
  assign nor_1_out = ~(A | B);  // NOR_Gate nor_1, 32 bits wide
  assign xor_1_out = A ^ B;  // XOR_Gate xor_1, 32 bits wide
  Multiplexer_part #(.width(32), .enable("false")) multiplexer_3 (
    .in0({32{1'b0}}), .in1(32'h1), .out(multiplexer_3_out), .sel(comparator_1_lt));
  Multiplexer_part #(.width(32), .enable("false")) multiplexer_4 (
    .in0({32{1'b0}}), .in1(32'h1), .out(multiplexer_4_out), .sel(comparator_2_lt));
  Multiplexer_part #(.width(32), .enable("false")) multiplexer_5 (
    .in0(multiplexer_3_out), .in1(multiplexer_4_out), .out(multiplexer_5_out), .sel(unSigned));
  Multiplexer_part #(.select(4), .width(32), .enable("false")) multiplexer_6 (
    .in0(adder_1_out), .in1(subtractor_1_out), .in4(and_3_out), .in5(or_2_out), .in6(nor_1_out),
    .in7(xor_1_out), .in8(multiplexer_5_out), .out(Output), .sel(Operation));  // open: in2, in3, in9, in10, in11, in12, in13, in14, in15
  not not_1 (not_1_out, L);
  assign Negative_Flags = not_1_out ? Output[31] : 1'bz;  // Controlled_Buffer controlled_buffer_1
  Negator #(.width(32)) negator_1 (.in(A), .out(A_prime));
  Negator #(.width(32)) negator_2 (.in(B), .out(B_prime));
  not not_2 (not_2_out, unSigned);
  and and_4 (and_4_out, not_2_out, A[31]);
  Multiplexer_part #(.width(32), .enable("false")) multiplexer_7 (
    .in0(A), .in1(A_prime), .out(multiplexer_7_out), .sel(and_4_out));
  Multiplexer_part #(.width(32), .enable("false")) multiplexer_8 (
    .in0(B), .in1(B_prime), .out(multiplexer_8_out), .sel(and_5_out));
  and and_5 (and_5_out, B[31], not_2_out);
  nor nor_2 (nor_2_out, Output[0], Output[1], Output[2], Output[3], Output[4], Output[5], Output[6], Output[7], Output[8], Output[9], Output[10], Output[11], Output[12], Output[13], Output[14], Output[15], Output[16], Output[17], Output[18], Output[19], Output[20], Output[21], Output[22], Output[23], Output[24], Output[25], Output[26], Output[27], Output[28], Output[29], Output[30], Output[31]);
  assign Zero_Flags = not_3_out ? nor_2_out : 1'bz;  // Controlled_Buffer controlled_buffer_2
  not not_3 (not_3_out, L);
  Divider #(.width(32)) divider_1 (
    .a(multiplexer_7_out), .b(multiplexer_8_out), .out(divider_1_out), .rem(Hi_t));  // open: upper
  Multiplexer_part #(.width(32), .enable("false")) multiplexer_9 (
    .in0(multiplier_1_out), .in1(mulu_1_lo), .out(Lo_star), .sel(unSigned));
  Multiplier #(.width(32)) multiplier_1 (.a(A), .b(B), .out(multiplier_1_out), .cout(multiplier_1_cout));  // open: cin
  Mulu mulu_1 (.A(A), .B(B), .Lo(mulu_1_lo), .Hi(mulu_1_hi));
  Multiplexer_part #(.width(32), .enable("false")) multiplexer_10 (
    .in0(multiplier_1_cout), .in1(mulu_1_hi), .out(Hi_star), .sel(unSigned));
  and and_6 (and_6_out, xor_2_out, not_4_out);
  Negator #(.width(32)) negator_3 (.in(divider_1_out), .out(negator_3_out));
  xor xor_2 (xor_2_out, A[31], B[31]);
  Multiplexer_part #(.width(32), .enable("false")) multiplexer_11 (
    .in0(divider_1_out), .in1(negator_3_out), .out(Lo_t), .sel(and_6_out));
  not not_4 (not_4_out, unSigned);

  // Other names for the same wires on the sheet: SigA = A[31]; SigB = B[31]; clk = Clock; NF = Negative_Flags;
  //   Op[3:0] = Operation; R[31:0] = Output; rst = Reset; uS = unSigned; ZF = Zero_Flags
endmodule

module Multiplexer (
  input  [31:0] I00,
  input  [31:0] I01,
  input  [31:0] I02,
  input  [31:0] I03,
  input  [31:0] I04,
  input  [31:0] I05,
  input  [31:0] I06,
  input  [31:0] I07,
  input  [31:0] I08,
  input  [31:0] I09,
  input  [31:0] I10,
  input  [31:0] I11,
  input  [31:0] I12,
  input  [31:0] I13,
  input  [31:0] I14,
  input  [31:0] I15,
  input  [31:0] I16,
  input  [31:0] I17,
  input  [31:0] I18,
  input  [31:0] I19,
  input  [31:0] I20,
  input  [31:0] I21,
  input  [31:0] I22,
  input  [31:0] I23,
  input  [31:0] I24,
  input  [31:0] I25,
  input  [31:0] I26,
  input  [31:0] I27,
  input  [31:0] I28,
  input  [31:0] I29,
  input  [31:0] I30,
  input  [31:0] I31,
  input  [4:0] Selector,
  output [31:0] Output
);

  wire L00, L01, L02, L03, L04, L05, L06, L07, L08, L09, L10, L11, L12, L13, L14, L15, L16, L17, L18, L19,
       L20, L21, L22, L23, L24, L25, L26, L27, L28, L29, L30, L31;

  assign Output = L00 ? I00 : 32'bz;  // Controlled_Buffer controlled_buffer_1
  assign Output = L05 ? I05 : 32'bz;  // Controlled_Buffer controlled_buffer_2
  assign Output = L10 ? I10 : 32'bz;  // Controlled_Buffer controlled_buffer_3
  assign Output = L15 ? I15 : 32'bz;  // Controlled_Buffer controlled_buffer_4
  assign Output = L20 ? I20 : 32'bz;  // Controlled_Buffer controlled_buffer_5
  assign Output = L25 ? I25 : 32'bz;  // Controlled_Buffer controlled_buffer_6
  assign Output = L27 ? I27 : 32'bz;  // Controlled_Buffer controlled_buffer_7
  assign Output = L29 ? I29 : 32'bz;  // Controlled_Buffer controlled_buffer_8
  assign Output = L31 ? I31 : 32'bz;  // Controlled_Buffer controlled_buffer_9
  assign Output = L01 ? I01 : 32'bz;  // Controlled_Buffer controlled_buffer_10
  assign Output = L06 ? I06 : 32'bz;  // Controlled_Buffer controlled_buffer_11
  assign Output = L11 ? I11 : 32'bz;  // Controlled_Buffer controlled_buffer_12
  assign Output = L16 ? I16 : 32'bz;  // Controlled_Buffer controlled_buffer_13
  assign Output = L21 ? I21 : 32'bz;  // Controlled_Buffer controlled_buffer_14
  assign Output = L26 ? I26 : 32'bz;  // Controlled_Buffer controlled_buffer_15
  assign Output = L28 ? I28 : 32'bz;  // Controlled_Buffer controlled_buffer_16
  assign Output = L30 ? I30 : 32'bz;  // Controlled_Buffer controlled_buffer_17
  Decoder #(.select(5), .enable("false")) decoder_1 (
    .out0(L00), .out1(L01), .out2(L02), .out3(L03), .out4(L04), .out5(L05), .out6(L06), .out7(L07),
    .out8(L08), .out9(L09), .out10(L10), .out11(L11), .out12(L12), .out13(L13), .out14(L14), .out15(L15),
    .out16(L16), .out17(L17), .out18(L18), .out19(L19), .out20(L20), .out21(L21), .out22(L22), .out23(L23),
    .out24(L24), .out25(L25), .out26(L26), .out27(L27), .out28(L28), .out29(L29), .out30(L30), .out31(L31),
    .sel(Selector));
  assign Output = L02 ? I02 : 32'bz;  // Controlled_Buffer controlled_buffer_18
  assign Output = L07 ? I07 : 32'bz;  // Controlled_Buffer controlled_buffer_19
  assign Output = L12 ? I12 : 32'bz;  // Controlled_Buffer controlled_buffer_20
  assign Output = L17 ? I17 : 32'bz;  // Controlled_Buffer controlled_buffer_21
  assign Output = L22 ? I22 : 32'bz;  // Controlled_Buffer controlled_buffer_22
  assign Output = L03 ? I03 : 32'bz;  // Controlled_Buffer controlled_buffer_23
  assign Output = L08 ? I08 : 32'bz;  // Controlled_Buffer controlled_buffer_24
  assign Output = L13 ? I13 : 32'bz;  // Controlled_Buffer controlled_buffer_25
  assign Output = L18 ? I18 : 32'bz;  // Controlled_Buffer controlled_buffer_26
  assign Output = L23 ? I23 : 32'bz;  // Controlled_Buffer controlled_buffer_27
  assign Output = L04 ? I04 : 32'bz;  // Controlled_Buffer controlled_buffer_28
  assign Output = L09 ? I09 : 32'bz;  // Controlled_Buffer controlled_buffer_29
  assign Output = L14 ? I14 : 32'bz;  // Controlled_Buffer controlled_buffer_30
  assign Output = L19 ? I19 : 32'bz;  // Controlled_Buffer controlled_buffer_31
  assign Output = L24 ? I24 : 32'bz;  // Controlled_Buffer controlled_buffer_32
endmodule

module Random (
  input  Clock,
  input  Enable,
  output [31:0] Random_Output
);

  Random_part #(.width(32)) random_1 (.clk(Clock), .next(Enable), .out(Random_Output));  // open: clr
endmodule

module Mulu (
  input  [31:0] A,
  input  [31:0] B,
  output [31:0] Lo,
  output [31:0] Hi
);

  wire C, C1_plus, C2_plus, C3_plus;
  wire [1:0] multiplier_1_out;
  wire [29:0] multiplier_1_out_2;
  wire [31:0] adder_1_out, adder_2_out, adder_3_out, adder_4_out, adder_5_out, adder_6_out,
       multiplexer_1_out, multiplexer_2_out, multiplexer_3_out, multiplexer_4_out, multiplier_1_cout;

  Multiplier #(.width(32)) multiplier_1 (
    .a({1'b0, A[31:1]}), .b({1'b0, B[31:1]}), .out({multiplier_1_out, multiplier_1_out_2}),
    .cout(multiplier_1_cout));  // open: cin
  and and_1 (C, A[0], B[0]);
  Multiplexer_part #(.width(32), .enable("false")) multiplexer_1 (
    .in0({multiplier_1_out_2, 2'b00}), .in1(adder_1_out), .out(multiplexer_1_out), .sel(B[0]));
  Adder #(.width(32)) adder_1 (
    .a({multiplier_1_out_2, 2'b00}), .b({A[31:1], 1'b0}), .out(adder_1_out), .cout(C1_plus));  // open: cin
  Multiplexer_part #(.width(32), .enable("false")) multiplexer_2 (
    .in0({multiplier_1_cout[29:0], multiplier_1_out}), .in1(adder_2_out), .out(multiplexer_2_out), .sel(B[0]));
  Adder #(.width(32)) adder_2 (
    .a({multiplier_1_cout[29:0], multiplier_1_out}), .b({32{1'b0}}), .out(adder_2_out), .cin(C1_plus));  // open: cout
  Adder #(.width(32)) adder_3 (
    .a(multiplexer_1_out), .b({B[31:1], 1'b0}), .out(adder_3_out), .cout(C2_plus));  // open: cin
  Adder #(.width(32)) adder_4 (.a(multiplexer_2_out), .b({32{1'b0}}), .out(adder_4_out), .cin(C2_plus));  // open: cout
  Multiplexer_part #(.width(32), .enable("false")) multiplexer_3 (
    .in0(multiplexer_1_out), .in1(adder_3_out), .out(multiplexer_3_out), .sel(A[0]));
  Multiplexer_part #(.width(32), .enable("false")) multiplexer_4 (
    .in0(multiplexer_2_out), .in1(adder_4_out), .out(multiplexer_4_out), .sel(A[0]));
  Adder #(.width(32)) adder_5 (.a(multiplexer_3_out), .b(32'h1), .out(adder_5_out), .cout(C3_plus));  // open: cin
  Adder #(.width(32)) adder_6 (.a(multiplexer_4_out), .b({32{1'b0}}), .out(adder_6_out), .cin(C3_plus));  // open: cout
  Multiplexer_part #(.width(32), .enable("false")) multiplexer_5 (
    .in0(multiplexer_3_out), .in1(adder_5_out), .out(Lo), .sel(C));
  Multiplexer_part #(.width(32), .enable("false")) multiplexer_6 (
    .in0(multiplexer_4_out), .in1(adder_6_out), .out(Hi), .sel(C));

  // Other names for the same wires on the sheet: CA = A[0]; CB = B[0]; A_prime[30:0] = A[31:1]; SA[31:1] = A[31:1];
  //   B_prime[30:0] = B[31:1]; SB[31:1] = B[31:1]
endmodule
